// Digital circuit CPU.dig as structural Verilog
module CPU (
  input  [15:0] A,
  input  [7:0] B,
  output [15:0] B_2,
  output [15:0] R0,
  output [15:0] R1,
  output [15:0] R2,
  output [15:0] R3
);

  wire button_1_out, button_2_out;
  wire [1:0] decoder_1_rd, decoder_1_rs, PC_out;
  wire [15:0] decoder_1_a, execute_1_result;
  wire [31:0] Program_d;

  Button button_1 (.out(button_1_out));
  Counter #(.Bits(2)) PC (.en(1'b1), .C(button_2_out), .clr(1'b0), .out(PC_out));  // open: ovf
  Button button_2 (.out(button_2_out));
  EEPROMDualPort #(.Bits(32)) Program (
    .A(PC_out), .Din({{8{1'b0}}, B, A}), .str(1'b1), .C(button_1_out), .ld(1'b1), .D(Program_d));
  Decoder decoder_1 (.Instruction(Program_d), .A(decoder_1_a), .rs(decoder_1_rs), .rd(decoder_1_rd));
  // Probe on nothing
  Execute execute_1 (.A(decoder_1_a), .B(B_2), .Result(execute_1_result));
  Register_File register_file_1 (
    .rs(decoder_1_rs), .rd(decoder_1_rd), .Result(execute_1_result), .Clock(button_2_out), .B(B_2), .R0(R0),
    .R1(R1), .R2(R2), .R3(R3));

  // Notes on the sheet:
  //   A: default 100
  //   B: default 1
  //   contents of Program (hex, n*v repeats v):
  //   10064,1200c8,230063,300022
endmodule
