// Digital circuit CPU.dig as structural Verilog
module CPU (
  input  [15:0] imm,
  input  [1:0] dest,
  input  [1:0] src,
  input  add,
  input  jump,
  output [15:0] B,
  output [15:0] R0,
  output [15:0] R1,
  output [15:0] R2,
  output [15:0] R3,
  output [1:0] rd,
  output [1:0] rs,
  output [15:0] A,
  output [1:0] PC
);

  wire Add_t, assembler_1_store_clk, button_1_out, Jump_t, Mode_out;
  wire [15:0] execute_1_result;
  wire [31:0] assembler_1_inst, Program_d;

  LED Programming (.in(Mode_out));
  DipSwitch Mode (.out(Mode_out));
  Assembler assembler_1 (
    .Mode(Mode_out), .imm(imm), .dest(dest), .src(src), .add(add), .jump(jump), .inst(assembler_1_inst),
    .store_clk(assembler_1_store_clk));
  Button button_1 (.out(button_1_out));
  CounterPreset #(.Bits(2), .isProgramCounter("true")) u_PC (
    .en(1'b1), .C(button_1_out), .dir(1'b0), .in(A[1:0]), .ld(Jump_t), .clr(1'b0), .out(PC));  // open: ovf
  EEPROMDualPort #(.Bits(32)) Program (
    .A(PC), .Din(assembler_1_inst), .str(1'b1), .C(assembler_1_store_clk), .ld(1'b1), .D(Program_d));
  Decoder decoder_1 (
    .Prog(Mode_out), .Bypass(assembler_1_inst), .Instruction(Program_d), .A(A), .rs(rs), .rd(rd),
    .add(Add_t), .jump(Jump_t));
  Execute execute_1 (.A(A), .B(B), .Add(Add_t), .Result(execute_1_result));
  Register_File register_file_1 (
    .rs(rs), .rd(rd), .Result(execute_1_result), .Clock(button_1_out), .B(B), .R0(R0), .R1(R1), .R2(R2),
    .R3(R3));

  // Notes on the sheet:
  //   contents of Program (hex, n*v repeats v):
  //   10064,1200c8,230063,300022
  //   =
  //   R
  //   +
  //   (
  //   )
endmodule
